// Logisim project bancoRegistrador.circ as structural Verilog
module main (
  input  [31:0] DataIn,
  input  DataIn_2,
  input  Reset,
  input  [31:0] DataOut
);

  D_Flip_Flop d_ff_1 (.clk(DataIn_2), .D(DataIn[31]), .Q(DataOut[31]), .reset(Reset));  // open: Qn, preset, en
  D_Flip_Flop d_ff_2 (.clk(DataIn_2), .D(DataIn[30]), .Q(DataOut[30]), .reset(Reset));  // open: Qn, preset, en
  D_Flip_Flop d_ff_3 (.clk(DataIn_2), .D(DataIn[29]), .Q(DataOut[29]), .reset(Reset));  // open: Qn, preset, en
  D_Flip_Flop d_ff_4 (.clk(DataIn_2), .D(DataIn[28]), .Q(DataOut[28]), .reset(Reset));  // open: Qn, preset, en
  D_Flip_Flop d_ff_5 (.clk(DataIn_2), .D(DataIn[27]), .Q(DataOut[27]), .reset(Reset));  // open: Qn, preset, en
  D_Flip_Flop d_ff_6 (.clk(DataIn_2), .D(DataIn[26]), .Q(DataOut[26]), .reset(Reset));  // open: Qn, preset, en
  D_Flip_Flop d_ff_7 (.clk(DataIn_2), .D(DataIn[25]), .Q(DataOut[25]), .reset(Reset));  // open: Qn, preset, en
  D_Flip_Flop d_ff_8 (.clk(DataIn_2), .D(DataIn[24]), .Q(DataOut[24]), .reset(Reset));  // open: Qn, preset, en
  D_Flip_Flop d_ff_9 (.clk(DataIn_2), .D(DataIn[23]), .Q(DataOut[23]), .reset(Reset));  // open: Qn, preset, en
  D_Flip_Flop d_ff_10 (.clk(DataIn_2), .D(DataIn[22]), .Q(DataOut[22]), .reset(Reset));  // open: Qn, preset, en
  D_Flip_Flop d_ff_11 (.clk(DataIn_2), .D(DataIn[21]), .Q(DataOut[21]), .reset(Reset));  // open: Qn, preset, en
  D_Flip_Flop d_ff_12 (.clk(DataIn_2), .D(DataIn[20]), .Q(DataOut[20]), .reset(Reset));  // open: Qn, preset, en
  D_Flip_Flop d_ff_13 (.clk(DataIn_2), .D(DataIn[19]), .Q(DataOut[19]), .reset(Reset));  // open: Qn, preset, en
  D_Flip_Flop d_ff_14 (.clk(DataIn_2), .D(DataIn[18]), .Q(DataOut[18]), .reset(Reset));  // open: Qn, preset, en
  D_Flip_Flop d_ff_15 (.clk(DataIn_2), .D(DataIn[17]), .Q(DataOut[17]), .reset(Reset));  // open: Qn, preset, en
  D_Flip_Flop d_ff_16 (.clk(DataIn_2), .D(DataIn[16]), .Q(DataOut[16]), .reset(Reset));  // open: Qn, preset, en
  D_Flip_Flop d_ff_17 (.clk(DataIn_2), .D(DataIn[15]), .Q(DataOut[15]), .reset(Reset));  // open: Qn, preset, en
  D_Flip_Flop d_ff_18 (.clk(DataIn_2), .D(DataIn[14]), .Q(DataOut[14]), .reset(Reset));  // open: Qn, preset, en
  D_Flip_Flop d_ff_19 (.clk(DataIn_2), .D(DataIn[13]), .Q(DataOut[13]), .reset(Reset));  // open: Qn, preset, en
  D_Flip_Flop d_ff_20 (.clk(DataIn_2), .D(DataIn[12]), .Q(DataOut[12]), .reset(Reset));  // open: Qn, preset, en
  D_Flip_Flop d_ff_21 (.clk(DataIn_2), .D(DataIn[11]), .Q(DataOut[11]), .reset(Reset));  // open: Qn, preset, en
  D_Flip_Flop d_ff_22 (.clk(DataIn_2), .D(DataIn[10]), .Q(DataOut[10]), .reset(Reset));  // open: Qn, preset, en
  D_Flip_Flop d_ff_23 (.clk(DataIn_2), .D(DataIn[9]), .Q(DataOut[9]), .reset(Reset));  // open: Qn, preset, en
  D_Flip_Flop d_ff_24 (.clk(DataIn_2), .D(DataIn[8]), .Q(DataOut[8]), .reset(Reset));  // open: Qn, preset, en
  D_Flip_Flop d_ff_25 (.clk(DataIn_2), .D(DataIn[7]), .Q(DataOut[7]), .reset(Reset));  // open: Qn, preset, en
  D_Flip_Flop d_ff_26 (.clk(DataIn_2), .D(DataIn[6]), .Q(DataOut[6]), .reset(Reset));  // open: Qn, preset, en
  D_Flip_Flop d_ff_27 (.clk(DataIn_2), .D(DataIn[5]), .Q(DataOut[5]), .reset(Reset));  // open: Qn, preset, en
  D_Flip_Flop d_ff_28 (.clk(DataIn_2), .D(DataIn[4]), .Q(DataOut[4]), .reset(Reset));  // open: Qn, preset, en
  D_Flip_Flop d_ff_29 (.clk(DataIn_2), .D(DataIn[3]), .Q(DataOut[3]), .reset(Reset));  // open: Qn, preset, en
  D_Flip_Flop d_ff_30 (.clk(DataIn_2), .D(DataIn[2]), .Q(DataOut[2]), .reset(Reset));  // open: Qn, preset, en
  D_Flip_Flop d_ff_31 (.clk(DataIn_2), .D(DataIn[1]), .Q(DataOut[1]), .reset(Reset));  // open: Qn, preset, en
  D_Flip_Flop d_ff_32 (.clk(DataIn_2), .D(DataIn[0]), .Q(DataOut[0]), .reset(Reset));  // open: Qn, preset, en
endmodule

module Registrador32bit (
  input  [31:0] DataIn,
  input  Save,
  input  Reset,
  output [31:0] DataOut
);

  D_Flip_Flop d_ff_1 (.clk(Save), .D(DataIn[31]), .Q(DataOut[31]), .reset(Reset));  // open: Qn, preset, en
  D_Flip_Flop d_ff_2 (.clk(Save), .D(DataIn[30]), .Q(DataOut[30]), .reset(Reset));  // open: Qn, preset, en
  D_Flip_Flop d_ff_3 (.clk(Save), .D(DataIn[29]), .Q(DataOut[29]), .reset(Reset));  // open: Qn, preset, en
  D_Flip_Flop d_ff_4 (.clk(Save), .D(DataIn[28]), .Q(DataOut[28]), .reset(Reset));  // open: Qn, preset, en
  D_Flip_Flop d_ff_5 (.clk(Save), .D(DataIn[27]), .Q(DataOut[27]), .reset(Reset));  // open: Qn, preset, en
  D_Flip_Flop d_ff_6 (.clk(Save), .D(DataIn[26]), .Q(DataOut[26]), .reset(Reset));  // open: Qn, preset, en
  D_Flip_Flop d_ff_7 (.clk(Save), .D(DataIn[25]), .Q(DataOut[25]), .reset(Reset));  // open: Qn, preset, en
  D_Flip_Flop d_ff_8 (.clk(Save), .D(DataIn[24]), .Q(DataOut[24]), .reset(Reset));  // open: Qn, preset, en
  D_Flip_Flop d_ff_9 (.clk(Save), .D(DataIn[23]), .Q(DataOut[23]), .reset(Reset));  // open: Qn, preset, en
  D_Flip_Flop d_ff_10 (.clk(Save), .D(DataIn[22]), .Q(DataOut[22]), .reset(Reset));  // open: Qn, preset, en
  D_Flip_Flop d_ff_11 (.clk(Save), .D(DataIn[21]), .Q(DataOut[21]), .reset(Reset));  // open: Qn, preset, en
  D_Flip_Flop d_ff_12 (.clk(Save), .D(DataIn[20]), .Q(DataOut[20]), .reset(Reset));  // open: Qn, preset, en
  D_Flip_Flop d_ff_13 (.clk(Save), .D(DataIn[19]), .Q(DataOut[19]), .reset(Reset));  // open: Qn, preset, en
  D_Flip_Flop d_ff_14 (.clk(Save), .D(DataIn[18]), .Q(DataOut[18]), .reset(Reset));  // open: Qn, preset, en
  D_Flip_Flop d_ff_15 (.clk(Save), .D(DataIn[17]), .Q(DataOut[17]), .reset(Reset));  // open: Qn, preset, en
  D_Flip_Flop d_ff_16 (.clk(Save), .D(DataIn[16]), .Q(DataOut[16]), .reset(Reset));  // open: Qn, preset, en
  D_Flip_Flop d_ff_17 (.clk(Save), .D(DataIn[15]), .Q(DataOut[15]), .reset(Reset));  // open: Qn, preset, en
  D_Flip_Flop d_ff_18 (.clk(Save), .D(DataIn[14]), .Q(DataOut[14]), .reset(Reset));  // open: Qn, preset, en
  D_Flip_Flop d_ff_19 (.clk(Save), .D(DataIn[13]), .Q(DataOut[13]), .reset(Reset));  // open: Qn, preset, en
  D_Flip_Flop d_ff_20 (.clk(Save), .D(DataIn[12]), .Q(DataOut[12]), .reset(Reset));  // open: Qn, preset, en
  D_Flip_Flop d_ff_21 (.clk(Save), .D(DataIn[11]), .Q(DataOut[11]), .reset(Reset));  // open: Qn, preset, en
  D_Flip_Flop d_ff_22 (.clk(Save), .D(DataIn[10]), .Q(DataOut[10]), .reset(Reset));  // open: Qn, preset, en
  D_Flip_Flop d_ff_23 (.clk(Save), .D(DataIn[9]), .Q(DataOut[9]), .reset(Reset));  // open: Qn, preset, en
  D_Flip_Flop d_ff_24 (.clk(Save), .D(DataIn[8]), .Q(DataOut[8]), .reset(Reset));  // open: Qn, preset, en
  D_Flip_Flop d_ff_25 (.clk(Save), .D(DataIn[7]), .Q(DataOut[7]), .reset(Reset));  // open: Qn, preset, en
  D_Flip_Flop d_ff_26 (.clk(Save), .D(DataIn[6]), .Q(DataOut[6]), .reset(Reset));  // open: Qn, preset, en
  D_Flip_Flop d_ff_27 (.clk(Save), .D(DataIn[5]), .Q(DataOut[5]), .reset(Reset));  // open: Qn, preset, en
  D_Flip_Flop d_ff_28 (.clk(Save), .D(DataIn[4]), .Q(DataOut[4]), .reset(Reset));  // open: Qn, preset, en
  D_Flip_Flop d_ff_29 (.clk(Save), .D(DataIn[3]), .Q(DataOut[3]), .reset(Reset));  // open: Qn, preset, en
  D_Flip_Flop d_ff_30 (.clk(Save), .D(DataIn[2]), .Q(DataOut[2]), .reset(Reset));  // open: Qn, preset, en
  D_Flip_Flop d_ff_31 (.clk(Save), .D(DataIn[1]), .Q(DataOut[1]), .reset(Reset));  // open: Qn, preset, en
  D_Flip_Flop d_ff_32 (.clk(Save), .D(DataIn[0]), .Q(DataOut[0]), .reset(Reset));  // open: Qn, preset, en
endmodule

module Banco32Reg32 (
  input  [31:0] Data,
  input  Reset,
  input  [31:0] ViewRegA,
  input  CLK,
  input  [4:0] RegA,
  input  [4:0] RegW,
  input  [31:0] ViewRegB,
  input  [4:0] RegB
);

  wire demultiplexer_1_out0, demultiplexer_1_out2;

  Demultiplexer #(.select(5), .enable("false")) demultiplexer_1 (
    .out0(demultiplexer_1_out0), .out1(Reset), .out2(demultiplexer_1_out2), .in(CLK), .sel(RegW));  // open: out3, out4, out5, out6, out7, out8, out9, out10, out11, out12, out13, out14, out15, out16, out17, out18, out19, out20, out21, out22, out23, out24, out25, out26, out27, out28, out29, out30, out31
  Registrador32bit registrador32bit_1 (.DataIn(Data), .Save(demultiplexer_1_out0), .Reset(Reset));  // open: DataOut
  Registrador32bit registrador32bit_2 (.DataIn(Data), .Save(Reset), .Reset(Reset));  // open: DataOut
  Registrador32bit registrador32bit_3 (.DataIn(Data), .Save(demultiplexer_1_out2), .Reset(Reset));  // open: DataOut
  Registrador32bit registrador32bit_4 (.DataIn(Data), .Reset(Reset));  // open: Save, DataOut
  Registrador32bit registrador32bit_5 (.DataIn(Data), .Reset(Reset));  // open: Save, DataOut
  Registrador32bit registrador32bit_6 (.DataIn(Data), .Reset(Reset));  // open: Save, DataOut
  Registrador32bit registrador32bit_7 (.DataIn(Data), .Reset(Reset));  // open: Save, DataOut
  Registrador32bit registrador32bit_8 (.DataIn(Data), .Reset(Reset));  // open: Save, DataOut
  Registrador32bit registrador32bit_9 (.DataIn(Data), .Reset(Reset));  // open: Save, DataOut
  Registrador32bit registrador32bit_10 (.DataIn(Data), .Reset(Reset));  // open: Save, DataOut
  Registrador32bit registrador32bit_11 (.DataIn(Data), .Reset(Reset));  // open: Save, DataOut
  Registrador32bit registrador32bit_12 (.DataIn(Data), .Reset(Reset));  // open: Save, DataOut
  Registrador32bit registrador32bit_13 (.DataIn(Data), .Reset(Reset));  // open: Save, DataOut
  Registrador32bit registrador32bit_14 (.DataIn(Data), .Reset(Reset));  // open: Save, DataOut
  Registrador32bit registrador32bit_15 (.DataIn(Data), .Reset(Reset));  // open: Save, DataOut
  Registrador32bit registrador32bit_16 (.DataIn(Data), .Reset(Reset));  // open: Save, DataOut
  Registrador32bit registrador32bit_17 (.DataIn(Data), .Reset(Reset));  // open: Save, DataOut
  Registrador32bit registrador32bit_18 (.DataIn(Data), .Reset(Reset));  // open: Save, DataOut
  Registrador32bit registrador32bit_19 (.DataIn(Data), .Reset(Reset));  // open: Save, DataOut
  Registrador32bit registrador32bit_20 (.DataIn(Data), .Reset(Reset));  // open: Save, DataOut
  Registrador32bit registrador32bit_21 (.DataIn(Data), .Reset(Reset));  // open: Save, DataOut
  Registrador32bit registrador32bit_22 (.DataIn(Data), .Reset(Reset));  // open: Save, DataOut
  Registrador32bit registrador32bit_23 (.DataIn(Data), .Reset(Reset));  // open: Save, DataOut
  Registrador32bit registrador32bit_24 (.DataIn(Data), .Reset(Reset));  // open: Save, DataOut
  Registrador32bit registrador32bit_25 (.DataIn(Data), .Reset(Reset));  // open: Save, DataOut
  Registrador32bit registrador32bit_26 (.DataIn(Data), .Reset(Reset));  // open: Save, DataOut
  Registrador32bit registrador32bit_27 (.DataIn(Data), .Reset(Reset));  // open: Save, DataOut
  Registrador32bit registrador32bit_28 (.DataIn(Data), .Reset(Reset));  // open: Save, DataOut
  Registrador32bit registrador32bit_29 (.DataIn(Data), .Reset(Reset));  // open: Save, DataOut
  Registrador32bit registrador32bit_30 (.DataIn(Data), .Reset(Reset));  // open: Save, DataOut
  Registrador32bit registrador32bit_31 (.DataIn(Data), .Reset(Reset));  // open: Save, DataOut
  Registrador32bit registrador32bit_32 (.DataIn(Data), .Reset(Reset));  // open: Save, DataOut
  Multiplexer #(.select(5), .width(32), .enable("false")) multiplexer_1 (
    .out(ViewRegA), .sel(RegA));  // open: in0, in1, in2, in3, in4, in5, in6, in7, in8, in9, in10, in11, in12, in13, in14, in15, in16, in17, in18, in19, in20, in21, in22, in23, in24, in25, in26, in27, in28, in29, in30, in31
  Multiplexer #(.select(5), .width(32), .enable("false")) multiplexer_2 (
    .out(ViewRegB), .sel(RegB));  // open: in0, in1, in2, in3, in4, in5, in6, in7, in8, in9, in10, in11, in12, in13, in14, in15, in16, in17, in18, in19, in20, in21, in22, in23, in24, in25, in26, in27, in28, in29, in30, in31
endmodule

module Reg16 (
  input  [15:0] DataIn,
  input  Entrada,
  input  Reset,
  output [15:0] DataOut
);

  D_Flip_Flop d_ff_1 (.clk(Entrada), .D(DataIn[15]), .Q(DataOut[15]), .reset(Reset));  // open: Qn, preset, en
  D_Flip_Flop d_ff_2 (.clk(Entrada), .D(DataIn[14]), .Q(DataOut[14]), .reset(Reset));  // open: Qn, preset, en
  D_Flip_Flop d_ff_3 (.clk(Entrada), .D(DataIn[13]), .Q(DataOut[13]), .reset(Reset));  // open: Qn, preset, en
  D_Flip_Flop d_ff_4 (.clk(Entrada), .D(DataIn[12]), .Q(DataOut[12]), .reset(Reset));  // open: Qn, preset, en
  D_Flip_Flop d_ff_5 (.clk(Entrada), .D(DataIn[11]), .Q(DataOut[11]), .reset(Reset));  // open: Qn, preset, en
  D_Flip_Flop d_ff_6 (.clk(Entrada), .D(DataIn[10]), .Q(DataOut[10]), .reset(Reset));  // open: Qn, preset, en
  D_Flip_Flop d_ff_7 (.clk(Entrada), .D(DataIn[9]), .Q(DataOut[9]), .reset(Reset));  // open: Qn, preset, en
  D_Flip_Flop d_ff_8 (.clk(Entrada), .D(DataIn[8]), .Q(DataOut[8]), .reset(Reset));  // open: Qn, preset, en
  D_Flip_Flop d_ff_9 (.clk(Entrada), .D(DataIn[7]), .Q(DataOut[7]), .reset(Reset));  // open: Qn, preset, en
  D_Flip_Flop d_ff_10 (.clk(Entrada), .D(DataIn[6]), .Q(DataOut[6]), .reset(Reset));  // open: Qn, preset, en
  D_Flip_Flop d_ff_11 (.clk(Entrada), .D(DataIn[5]), .Q(DataOut[5]), .reset(Reset));  // open: Qn, preset, en
  D_Flip_Flop d_ff_12 (.clk(Entrada), .D(DataIn[4]), .Q(DataOut[4]), .reset(Reset));  // open: Qn, preset, en
  D_Flip_Flop d_ff_13 (.clk(Entrada), .D(DataIn[3]), .Q(DataOut[3]), .reset(Reset));  // open: Qn, preset, en
  D_Flip_Flop d_ff_14 (.clk(Entrada), .D(DataIn[2]), .Q(DataOut[2]), .reset(Reset));  // open: Qn, preset, en
  D_Flip_Flop d_ff_15 (.clk(Entrada), .D(DataIn[1]), .Q(DataOut[1]), .reset(Reset));  // open: Qn, preset, en
  D_Flip_Flop d_ff_16 (.clk(Entrada), .D(DataIn[0]), .Q(DataOut[0]), .reset(Reset));  // open: Qn, preset, en
endmodule
