// Logisim project ula.circ as structural Verilog
module mux32 (
  input  e0,
  input  e1,
  input  e2,
  input  e3,
  input  e4,
  input  e5,
  input  e6,
  input  e7,
  input  e8,
  input  e9,
  input  e10,
  input  e11,
  input  e12,
  input  e13,
  input  e14,
  input  e15,
  input  e16,
  input  e17,
  input  e18,
  input  e19,
  input  e20,
  input  e21,
  input  e22,
  input  e23,
  input  e24,
  input  e25,
  input  e26,
  input  e27,
  input  e28,
  input  e29,
  input  e30,
  input  e31,
  input  sel4,
  input  se3,
  input  sel2,
  input  sel1,
  input  sel0,
  output Saida
);

  wire and_1_out, and_2_out, and_3_out, and_4_out, and_5_out, and_6_out, and_7_out, and_8_out, and_9_out,
       and_10_out, and_11_out, and_12_out, and_13_out, and_14_out, and_15_out, and_16_out, and_17_out,
       and_18_out, and_19_out, and_20_out, and_21_out, and_22_out, and_23_out, and_24_out, and_25_out,
       and_26_out, and_27_out, and_28_out, and_29_out, and_30_out, and_31_out, and_32_out;

  and and_1 (and_1_out, e0, ~sel4, ~se3, ~sel2, ~sel1, ~sel0);  // AND_Gate
  and and_2 (and_2_out, e1, ~sel4, ~se3, ~sel2, ~sel1, sel0);  // AND_Gate
  and and_3 (and_3_out, e2, ~sel4, ~se3, ~sel2, sel1, ~sel0);  // AND_Gate
  and and_4 (and_4_out, e3, ~sel4, ~se3, ~sel2, sel1, sel0);  // AND_Gate
  and and_5 (and_5_out, e4, ~sel4, ~se3, sel2, ~sel1, ~sel0);  // AND_Gate
  and and_6 (and_6_out, e5, ~sel4, ~se3, sel2, ~sel1, sel0);  // AND_Gate
  and and_7 (and_7_out, e6, ~sel4, ~se3, sel2, sel1, ~sel0);  // AND_Gate
  and and_8 (and_8_out, e7, ~sel4, ~se3, sel2, sel1, sel0);  // AND_Gate
  and and_9 (and_9_out, e8, ~sel4, se3, ~sel2, ~sel1, ~sel0);  // AND_Gate
  and and_10 (and_10_out, e9, ~sel4, se3, ~sel2, ~sel1, sel0);  // AND_Gate
  and and_11 (and_11_out, e10, ~sel4, se3, ~sel2, sel1, ~sel0);  // AND_Gate
  and and_12 (and_12_out, e11, ~sel4, se3, ~sel2, sel1, sel0);  // AND_Gate
  and and_13 (and_13_out, e12, ~sel4, se3, sel2, ~sel1, ~sel0);  // AND_Gate
  and and_14 (and_14_out, e13, ~sel4, se3, sel2, ~sel1, sel0);  // AND_Gate
  and and_15 (and_15_out, e14, ~sel4, se3, sel2, sel1, ~sel0);  // AND_Gate
  and and_16 (and_16_out, e15, ~sel4, se3, sel2, sel1, sel0);  // AND_Gate
  and and_17 (and_17_out, e16, sel4, ~se3, ~sel2, ~sel1, ~sel0);  // AND_Gate
  and and_18 (and_18_out, e17, sel4, ~se3, ~sel2, ~sel1, sel0);  // AND_Gate
  and and_19 (and_19_out, e18, sel4, ~se3, ~sel2, sel1, ~sel0);  // AND_Gate
  and and_20 (and_20_out, e19, sel4, ~se3, ~sel2, sel1, sel0);  // AND_Gate
  and and_21 (and_21_out, e20, sel4, ~se3, sel2, ~sel1, ~sel0);  // AND_Gate
  and and_22 (and_22_out, e21, sel4, ~se3, sel2, ~sel1, sel0);  // AND_Gate
  and and_23 (and_23_out, e22, sel4, ~se3, sel2, sel1, ~sel0);  // AND_Gate
  and and_24 (and_24_out, e23, sel4, ~se3, sel2, sel1, sel0);  // AND_Gate
  and and_25 (and_25_out, e24, sel4, se3, ~sel2, ~sel1, ~sel0);  // AND_Gate
  and and_26 (and_26_out, e25, sel4, se3, ~sel2, ~sel1, sel0);  // AND_Gate
  and and_27 (and_27_out, e26, sel4, se3, ~sel2, sel1, ~sel0);  // AND_Gate
  and and_28 (and_28_out, e27, sel4, se3, ~sel2, sel1, sel0);  // AND_Gate
  and and_29 (and_29_out, e28, sel4, se3, sel2, ~sel1, ~sel0);  // AND_Gate
  and and_30 (and_30_out, e29, sel4, se3, sel2, ~sel1, sel0);  // AND_Gate
  and and_31 (and_31_out, e30, sel4, se3, sel2, sel1, ~sel0);  // AND_Gate
  and and_32 (and_32_out, e31, sel4, se3, sel2, sel1, sel0);
  or or_1 (Saida, and_1_out, and_2_out, and_3_out, and_4_out, and_5_out, and_6_out, and_7_out, and_8_out, and_9_out, and_10_out, and_11_out, and_12_out, and_13_out, and_14_out, and_15_out, and_16_out, and_17_out, and_18_out, and_19_out, and_20_out, and_21_out, and_22_out, and_23_out, and_24_out, and_25_out, and_26_out, and_27_out, and_28_out, and_29_out, and_30_out, and_31_out, and_32_out);
endmodule

module somador1bit (
  input  vem1,
  input  a,
  input  b,
  output s,
  output vai1
);

  wire and_1_out, and_2_out, and_3_out, and_4_out, and_5_out, and_6_out, and_7_out;

  and and_1 (and_1_out, ~a, ~b, vem1);  // AND_Gate
  and and_2 (and_2_out, ~a, b, ~vem1);  // AND_Gate
  and and_3 (and_3_out, a, ~b, ~vem1);  // AND_Gate
  and and_4 (and_4_out, ~a, b, vem1);  // AND_Gate
  and and_5 (and_5_out, a, ~b, vem1);  // AND_Gate
  and and_6 (and_6_out, a, b, ~vem1);  // AND_Gate
  and and_7 (and_7_out, a, b, vem1);
  or or_1 (s, and_1_out, and_2_out, and_3_out, and_4_out);
  or or_2 (vai1, and_4_out, and_5_out, and_6_out, and_7_out);
endmodule

module somador32 (
  input  vem31,
  input  a31,
  input  a0,
  input  a0_2,
  input  a0_3,
  input  a0_4,
  input  a0_5,
  input  a0_6,
  input  a0_7,
  input  a0_8,
  input  a0_9,
  input  a0_10,
  input  a0_11,
  input  a0_12,
  input  a0_13,
  input  a0_14,
  input  a0_15,
  input  a0_16,
  input  a0_17,
  input  a0_18,
  input  a0_19,
  input  a0_20,
  input  a0_21,
  input  a0_22,
  input  a0_23,
  input  a0_24,
  input  a0_25,
  input  a0_26,
  input  a0_27,
  input  a0_28,
  input  a0_29,
  input  a0_30,
  input  a0_31,
  input  b31,
  input  b0,
  input  b0_2,
  input  b0_3,
  input  b0_4,
  input  b0_5,
  input  b0_6,
  input  b0_7,
  input  b0_8,
  input  b0_9,
  input  b0_10,
  input  b0_11,
  input  b0_12,
  input  b0_13,
  input  b0_14,
  input  b0_15,
  input  b0_16,
  input  b0_17,
  input  b0_18,
  input  b0_19,
  input  b0_20,
  input  b0_21,
  input  b0_22,
  input  b0_23,
  input  b0_24,
  input  b0_25,
  input  b0_26,
  input  b0_27,
  input  b0_28,
  input  b0_29,
  input  b0_30,
  input  b0_31,
  output s31,
  output s31_2,
  output s31_3,
  output s31_4,
  output s31_5,
  output s31_6,
  output s31_7,
  output s31_8,
  output s31_9,
  output s31_10,
  output s31_11,
  output s31_12,
  output s31_13,
  output s31_14,
  output s31_15,
  output s31_16,
  output s31_17,
  output s31_18,
  output s31_19,
  output s31_20,
  output s31_21,
  output s31_22,
  output s31_23,
  output s31_24,
  output s31_25,
  output s31_26,
  output s31_27,
  output s31_28,
  output s31_29,
  output s31_30,
  output s31_31,
  output s0
);

  wire somador1bit_1_vai1, somador1bit_2_vai1, somador1bit_3_vai1, somador1bit_4_vai1, somador1bit_5_vai1,
       somador1bit_6_vai1, somador1bit_7_vai1, somador1bit_8_vai1, somador1bit_9_vai1, somador1bit_10_vai1,
       somador1bit_11_vai1, somador1bit_12_vai1, somador1bit_13_vai1, somador1bit_14_vai1,
       somador1bit_15_vai1, somador1bit_16_vai1, somador1bit_17_vai1, somador1bit_18_vai1,
       somador1bit_19_vai1, somador1bit_20_vai1, somador1bit_21_vai1, somador1bit_22_vai1,
       somador1bit_23_vai1, somador1bit_24_vai1, somador1bit_25_vai1, somador1bit_26_vai1,
       somador1bit_27_vai1, somador1bit_28_vai1, somador1bit_29_vai1, somador1bit_30_vai1,
       somador1bit_31_vai1, somador1bit_32_vai1;

  somador1bit somador1bit_1 (.a(a31), .b(b31), .vem1(vem31), .vai1(somador1bit_1_vai1), .s(s31));
  somador1bit somador1bit_2 (.a(a0), .b(b0), .vem1(somador1bit_1_vai1), .vai1(somador1bit_2_vai1), .s(s31_2));
  somador1bit somador1bit_3 (.a(a0_2), .b(b0_2), .vem1(somador1bit_2_vai1), .vai1(somador1bit_3_vai1), .s(s31_3));
  somador1bit somador1bit_4 (.a(a0_3), .b(b0_3), .vem1(somador1bit_3_vai1), .vai1(somador1bit_4_vai1), .s(s31_4));
  somador1bit somador1bit_5 (.a(a0_4), .b(b0_4), .vem1(somador1bit_4_vai1), .vai1(somador1bit_5_vai1), .s(s31_5));
  somador1bit somador1bit_6 (.a(a0_5), .b(b0_5), .vem1(somador1bit_5_vai1), .vai1(somador1bit_6_vai1), .s(s31_6));
  somador1bit somador1bit_7 (.a(a0_6), .b(b0_6), .vem1(somador1bit_6_vai1), .vai1(somador1bit_7_vai1), .s(s31_7));
  somador1bit somador1bit_8 (.a(a0_7), .b(b0_7), .vem1(somador1bit_7_vai1), .vai1(somador1bit_8_vai1), .s(s31_8));
  somador1bit somador1bit_9 (.a(a0_8), .b(b0_8), .vem1(somador1bit_8_vai1), .vai1(somador1bit_9_vai1), .s(s31_9));
  somador1bit somador1bit_10 (.a(a0_9), .b(b0_9), .vem1(somador1bit_9_vai1), .vai1(somador1bit_10_vai1), .s(s31_10));
  somador1bit somador1bit_11 (.a(a0_10), .b(b0_10), .vem1(somador1bit_10_vai1), .vai1(somador1bit_11_vai1), .s(s31_11));
  somador1bit somador1bit_12 (.a(a0_12), .b(b0_12), .vem1(somador1bit_13_vai1), .vai1(somador1bit_12_vai1), .s(s31_13));
  somador1bit somador1bit_13 (.a(a0_11), .b(b0_11), .vem1(somador1bit_11_vai1), .vai1(somador1bit_13_vai1), .s(s31_12));
  somador1bit somador1bit_14 (.a(a0_13), .b(b0_13), .vem1(somador1bit_12_vai1), .vai1(somador1bit_14_vai1), .s(s31_14));
  somador1bit somador1bit_15 (.a(a0_14), .b(b0_14), .vem1(somador1bit_14_vai1), .vai1(somador1bit_15_vai1), .s(s31_15));
  somador1bit somador1bit_16 (.a(a0_15), .b(b0_15), .vem1(somador1bit_15_vai1), .vai1(somador1bit_16_vai1), .s(s31_16));
  somador1bit somador1bit_17 (.a(a0_16), .b(b0_16), .vem1(somador1bit_16_vai1), .vai1(somador1bit_17_vai1), .s(s31_17));
  somador1bit somador1bit_18 (.a(a0_17), .b(b0_17), .vem1(somador1bit_17_vai1), .vai1(somador1bit_18_vai1), .s(s31_18));
  somador1bit somador1bit_19 (.a(a0_18), .b(b0_18), .vem1(somador1bit_18_vai1), .vai1(somador1bit_19_vai1), .s(s31_19));
  somador1bit somador1bit_20 (.a(a0_20), .b(b0_20), .vem1(somador1bit_21_vai1), .vai1(somador1bit_20_vai1), .s(s31_21));
  somador1bit somador1bit_21 (.a(a0_19), .b(b0_19), .vem1(somador1bit_19_vai1), .vai1(somador1bit_21_vai1), .s(s31_20));
  somador1bit somador1bit_22 (.a(a0_21), .b(b0_21), .vem1(somador1bit_20_vai1), .vai1(somador1bit_22_vai1), .s(s31_22));
  somador1bit somador1bit_23 (.a(a0_22), .b(b0_22), .vem1(somador1bit_22_vai1), .vai1(somador1bit_23_vai1), .s(s31_23));
  somador1bit somador1bit_24 (.a(a0_23), .b(b0_23), .vem1(somador1bit_23_vai1), .vai1(somador1bit_24_vai1), .s(s31_24));
  somador1bit somador1bit_25 (.a(a0_24), .b(b0_24), .vem1(somador1bit_24_vai1), .vai1(somador1bit_25_vai1), .s(s31_25));
  somador1bit somador1bit_26 (.a(a0_25), .b(b0_25), .vem1(somador1bit_25_vai1), .vai1(somador1bit_26_vai1), .s(s31_26));
  somador1bit somador1bit_27 (.a(a0_26), .b(b0_26), .vem1(somador1bit_26_vai1), .vai1(somador1bit_27_vai1), .s(s31_27));
  somador1bit somador1bit_28 (.a(a0_28), .b(b0_28), .vem1(somador1bit_29_vai1), .vai1(somador1bit_28_vai1), .s(s31_29));
  somador1bit somador1bit_29 (.a(a0_27), .b(b0_27), .vem1(somador1bit_27_vai1), .vai1(somador1bit_29_vai1), .s(s31_28));
  somador1bit somador1bit_30 (.a(a0_29), .b(b0_29), .vem1(somador1bit_28_vai1), .vai1(somador1bit_30_vai1), .s(s31_30));
  somador1bit somador1bit_31 (.a(a0_30), .b(b0_30), .vem1(somador1bit_30_vai1), .vai1(somador1bit_31_vai1), .s(s31_31));
  somador1bit somador1bit_32 (.a(a0_31), .b(b0_31), .vem1(somador1bit_31_vai1), .vai1(somador1bit_32_vai1), .s(s0));
  // also tied to GND on the sheet: somador1bit_32_vai1
endmodule

module shiftlogicalleft32 (
  input  [31:0] in_1,
  input  s,
  output [31:0] out_3
);

  mux2_32bit mux2_32bit_1 (.a(in_1), .in_2({in_1[30:0], 1'b0}), .sel(s), .s(out_3));
endmodule

module mux2_32bit (
  input  [31:0] a,
  input  [31:0] in_2,
  input  sel,
  output [31:0] s
);

  wire [31:0] and_1_out, and_2_out;

  assign and_1_out = a & ~{32{sel}};  // AND_Gate and_1, 32 bits wide
  assign and_2_out = in_2 & {32{sel}};  // AND_Gate and_2, 32 bits wide
  assign s = and_1_out | and_2_out;  // OR_Gate or_1, 32 bits wide
endmodule
